# Fritzing sketch scheme (saved by Fritzing 0.9.6b)
breadboards: 2

parts:
  M1 = DOIT Esp32 DevKit v1 (30 pins long, 11 pins width) [part_number=ESP32S-PIN30]
  Grove1 = Grove OLED 128x96
  S1 = Pushbutton [package="[SMD]"]
  S2 = Pushbutton [package="[SMD]"]

nets:
  3V3: M1.3V3, Grove1.VCC
  GND: M1.GND, Grove1.GND, S1.Pin_3, S1.Pin_4, S2.Pin_3, S2.Pin_4
  N1: M1.D4, S1.Pin_1, S1.Pin_2
  N2: M1.D5, S2.Pin_1, S2.Pin_2
  N3: M1.D21, Grove1.SDA
  N4: M1.D22, Grove1.SCL

custom parts:
  DOIT Esp32 DevKit v1 (30 pins long, 11 pins width): The DOIT Esp32 DevKit v1 is one of the development board created by DOIT to evaluate the ESP-WROOM-32 module. It is based on the ESP32 microcontroller that boasts Wifi, Bluetooth, Ethernet and Low Power support all in a single chip. (vanepp) made breadboard work, adjusted pin numbering and labels and reduced size of schematic and cleaned up pcb. This chip is 30pins long (2 x15) and 11 pins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
