# Fritzing sketch scheme (saved by Fritzing 0.9.6b)
breadboards: 2

parts:
  M1 = DOIT Esp32 DevKit v1 (30 pins long, 11 pins width) [part_number=ESP32S-PIN30]
  Grove1 = Grove OLED 128x96
  HC-SR04_Sensor_1 = HC-SR04 Ultrasonic Distance Sensor
  A1 = am312 pir sensor [package=THT]
  S1 = Pushbutton [package="[THT]"]
  R1 = Resistor [tolerance=±5% resistance=1k package="2512 [SMD]"]
  R2 = Resistor [tolerance=±5% resistance=220 package="0805 [SMD]"]

nets:
  3V3: M1.3V3, Grove1.VCC, A1.pin1
  GND: M1.GND, Grove1.GND, HC-SR04_Sensor_1.GND, A1.pin3, S1.Pin_3, S1.Pin_4, R2.Pin_1
  N1: M1.D4, S1.Pin_1, S1.Pin_2
  N2: M1.D5, HC-SR04_Sensor_1.TRIG
  N3: M1.D18, HC-SR04_Sensor_1.ECHO, R1.Pin_0, R1.Pin_1, R2.Pin_0
  N4: M1.D21, Grove1.SDA
  N5: M1.D22, Grove1.SCL
  N6: M1.D27, A1.pin2
  VIN: M1.VIN, HC-SR04_Sensor_1.VCC

custom parts:
  DOIT Esp32 DevKit v1 (30 pins long, 11 pins width): The DOIT Esp32 DevKit v1 is one of the development board created by DOIT to evaluate the ESP-WROOM-32 module. It is based on the ESP32 microcontroller that boasts Wifi, Bluetooth, Ethernet and Low Power support all in a single chip. (vanepp) made breadboard work, adjusted pin numbering and labels and reduced size of schematic and cleaned up pcb. This chip is 30pins long (2 x15) and 11 pins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
  am312 pir sensor: The AM312 is an ultra-miniature PIR module which uses a pyroelectric sensor similar to the one found in the common SR501 but in a more compact form factor.
