# Fritzing sketch scheme (saved by Fritzing 0.9.6b)
breadboards: 2

parts:
  M1 = DOIT Esp32 DevKit v1 (30 pins long, 11 pins width) [part_number=ESP32S-PIN30]
  HC-SR04_Sensor_1 = HC-SR04 Ultrasonic Distance Sensor
  Grove2 = Grove OLED 128x96
  R1 = Resistor [tolerance=±5% power=0.25 resistance=1k package=THT]
  R2 = Resistor [tolerance=±5% power=0.25 resistance=2.2k package=THT]
  R3 = Photocell (LDR) [package=THT]
  R4 = Resistor [tolerance=±5% power=0.25 resistance=10k package=THT]
  J1 = Piezo Speaker
  Q1 = NPN-Transistor [package="TO92 [THT]"]
  R5 = Resistor [tolerance=±5% power=0.25 resistance=1k package=THT]
  A1 = am312 pir sensor [package=THT]
  S1 = Pushbutton [package="[SMD]"]
  LED1 = smd LED [color="Red (633nm)" package="0805 [SMD]"]
  R6 = Resistor [tolerance=±5% power=0.25 resistance=220 package=THT]

nets:
  3V3: M1.3V3, Grove2.VCC, R3.pin_0, J1.pin2, A1.pin1
  GND: M1.GND, HC-SR04_Sensor_1.GND, Grove2.GND, R4.Pin_1, A1.pin3, S1.Pin_3, S1.Pin_4, LED1.cathode, R6.Pin_0, R6.Pin_1
  N1: M1.D15, LED1.anode
  N2: M1.D4, S1.Pin_1, S1.Pin_2
  N3: M1.D5, HC-SR04_Sensor_1.TRIG
  N4: M1.D18, HC-SR04_Sensor_1.ECHO, R1.Pin_0, R1.Pin_1, R2.Pin_0
  N5: M1.D21, Grove2.SDA
  N6: M1.D22, Grove2.SCL
  N7: M1.D34, R3.pin_1, R4.Pin_0
  N8: M1.D12, R5.Pin_1
  N9: M1.D13, A1.pin2
  VIN: M1.VIN, HC-SR04_Sensor_1.VCC
  N10: Q1.B, R5.Pin_0

custom parts:
  DOIT Esp32 DevKit v1 (30 pins long, 11 pins width): The DOIT Esp32 DevKit v1 is one of the development board created by DOIT to evaluate the ESP-WROOM-32 module. It is based on the ESP32 microcontroller that boasts Wifi, Bluetooth, Ethernet and Low Power support all in a single chip. (vanepp) made breadboard work, adjusted pin numbering and labels and reduced size of schematic and cleaned up pcb. This chip is 30pins long (2 x15) and 11 pins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
  am312 pir sensor: The AM312 is an ultra-miniature PIR module which uses a pyroelectric sensor similar to the one found in the common SR501 but in a more compact form factor.
