# Fritzing sketch player (saved by Fritzing 0.9.6b)
breadboards: 2

parts:
  M1 = DOIT Esp32 DevKit v1 (30 pins long, 11 pins width) [part_number=ESP32S-PIN30]
  microSD1 = MicroSD Card Module
  Компонент1 = Adafruit MAX98357A I2S 3W Class D Amplifier [part_number="Adafruit #3006"]
  SP1 = SPEAKER [package=pcb_mount_speaker]
  Grove1 = Grove OLED 128x96
  S1 = Pushbutton [package="[SMD]"]
  S2 = Pushbutton [package="[SMD]"]
  S3 = Pushbutton [package="[SMD]"]

nets:
  3V3: M1.3V3, Grove1.VCC
  GND: M1.GND, microSD1.GND, Компонент1.GND, Grove1.GND
  N1: M1.D5, microSD1.CS
  N2: M1.D18, microSD1.SCK
  N3: M1.D19, microSD1.MISO
  N4: M1.D21, Grove1.SDA
  N5: M1.D22, Grove1.SCL
  N6: M1.D23, microSD1.MOSI
  N7: M1.D25, Компонент1.LRCLK
  N8: M1.D26, Компонент1.BCLK
  N9: M1.D27, Компонент1.DIN
  N10: M1.D14, S1.Pin_1, S1.Pin_2
  N11: M1.D12, S3.Pin_3, S3.Pin_4
  N12: M1.D13, S2.Pin_1, S2.Pin_2
  VIN: M1.VIN, microSD1.VCC, Компонент1.VIN
  N13: Компонент1.VO-, SP1.+
  N14: Компонент1.VO+, SP1.-
  N15: S1.Pin_3, S1.Pin_4, S2.Pin_3, S2.Pin_4, S3.Pin_1, S3.Pin_2

custom parts:
  DOIT Esp32 DevKit v1 (30 pins long, 11 pins width): The DOIT Esp32 DevKit v1 is one of the development board created by DOIT to evaluate the ESP-WROOM-32 module. It is based on the ESP32 microcontroller that boasts Wifi, Bluetooth, Ethernet and Low Power support all in a single chip. (vanepp) made breadboard work, adjusted pin numbering and labels and reduced size of schematic and cleaned up pcb. This chip is 30pins long (2 x15) and 11 pins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
  Adafruit MAX98357A I2S 3W Class D Amplifier: Listen to this good news - we now have an all in one digital audio amp breakout board that works incredibly well with the Raspberry Pi! If you're looking for an easy and low cost way to get you digital sound files bumpin' then the MAX08357 I2S Amp Breakout is for you. It takes standard I2S digital audio input and, not only decodes it into analog, but also amplifies it directly into a speaker.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
