# Fritzing sketch scheme (saved by Fritzing 0.9.6b)
breadboards: 2

parts:
  M1 = DOIT Esp32 DevKit v1 (30 pins long, 11 pins width) [part_number=ESP32S-PIN30]
  SERVO1 = Tower Pro SG90 servo [part_number=101246]
  HC-SR04_Sensor_1 = HC-SR04 Ultrasonic Distance Sensor
  R1 = Resistor [tolerance=±5% resistance=10k package="1206 [SMD]"]
  R2 = Resistor [tolerance=±5% resistance=22k package="2010 [SMD]"]
  A1 = am312 pir sensor [package=THT]
  Grove1 = Grove OLED 128x96

nets:
  3V3: M1.3V3, Grove1.VCC
  GND: M1.GND, SERVO1.GND, HC-SR04_Sensor_1.GND, R2.Pin_0, A1.pin3, Grove1.GND
  N1: M1.D21, Grove1.SDA
  N2: M1.D22, Grove1.SCL
  N3: M1.D26, R1.Pin_0, R2.Pin_1
  N4: M1.D27, SERVO1.Signal
  N5: M1.D14, A1.pin2
  N6: M1.D13, HC-SR04_Sensor_1.TRIG
  VIN: M1.VIN, SERVO1.+5V, HC-SR04_Sensor_1.VCC, A1.pin1
  N7: HC-SR04_Sensor_1.ECHO, R1.Pin_1

notes:
  Схема подключения:
  Servo SG-90:
  1) GND - GND
  2) VCC - 5v
  3) SIG - D27 esp
  HC-SR04:
  1) VCC - 5v
  2) GND - GND
  3) TRIG - D13 esp
  4) (ECHO - resis 10kOm - D26 esp) - resis 20kOm - GND
  PIR AM312:
  1) VCC - 5v
  2) GND - GND
  3) OUT - D14 esp
  Dislplay oled:
  1) VCC - 3.3v
  2) GND - GND
  3) SCL - D22 esp
  4) SDA - D21 esp

custom parts:
  DOIT Esp32 DevKit v1 (30 pins long, 11 pins width): The DOIT Esp32 DevKit v1 is one of the development board created by DOIT to evaluate the ESP-WROOM-32 module. It is based on the ESP32 microcontroller that boasts Wifi, Bluetooth, Ethernet and Low Power support all in a single chip. (vanepp) made breadboard work, adjusted pin numbering and labels and reduced size of schematic and cleaned up pcb. This chip is 30pins long (2 x15) and 11 pins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
  Tower Pro SG90 servo: Original file by John De Cristofaro http://www.adafruit.com/products/1449 Adafruit Feedback Servo (Small) Edited by: e-radionica.com 28/9/2015
  am312 pir sensor: The AM312 is an ultra-miniature PIR module which uses a pyroelectric sensor similar to the one found in the common SR501 but in a more compact form factor.
